# Fritzing sketch connections (saved by Fritzing 0.9.4)
stripboards: 1

parts:
  Bauteil1 = Arduino Nano 33 IOT
  Capacitive_Soil_Moisture_Sensor1 = DFRobot Capacitive Soil Moisture Sensor V1.0 [part_number=SEN0193]
  Grove_Relay1 = Grove Relay
  Power_plug1 = Power plug
  Capacitive_Soil_Moisture_Sensor2 = DFRobot Capacitive Soil Moisture Sensor V1.0 [part_number=SEN0193]
  S1 = Reed switch [package=THT]

nets:
  GND: Bauteil1.GND, Bauteil1.D13~, Power_plug1.GND
  N1: Bauteil1.D4, Grove_Relay1.SIG
  VIN: Bauteil1.VIN, Power_plug1.VCC
  N2: Bauteil1.A1, Capacitive_Soil_Moisture_Sensor2.A
  VCC: Capacitive_Soil_Moisture_Sensor1.VCC, Grove_Relay1.VCC, Capacitive_Soil_Moisture_Sensor2.VCC
  GND_2: Grove_Relay1.GND, Capacitive_Soil_Moisture_Sensor2.GND, S1.pin_2

custom parts:
  Arduino Nano 33 IOT: The Arduino Nano 33 IoT is the easiest and cheapest point of entry to enhance existing devices (and creating new ones) to be part of the IoT and designing pico-network applications. Whether you are looking at building a sensor network connected to your office or home router, or if you want to create a BLE device sending data to a cellphone, the Nano 33 IoT is your one-stop-solution for many of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
  DFRobot Capacitive Soil Moisture Sensor V1.0: DFRobot Capacitive Soil Moisture Sensor V1.0 This product measures soil moisture levels by capacitive sensing, rather than resistive sensing like other types of moisture sensor. It is made of a corrosion resistant material giving it a long service life. Insert it into soil and impress your friends with the real-time soil moisture data! The product includes an on-board voltage regulator which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
  Grove Relay: Relay, Grove connector.
